# Fritzing sketch RunnerGame-Circuit (saved by Fritzing 0.9.3b)
breadboards: 1

parts:
  Pico_H1 = Raspberry Pi Pico H
  J1 = Generic male header - 4 pins [form="♂ (male)" package=THT]
  S1 = Momentary Switch [package=ksa_sealed_tac_switch]
  S2 = Momentary Switch [package=ksa_sealed_tac_switch]
  J2 = Piezo Speaker

nets:
  GND: Pico_H1.GND, J1.GND, J2.pin1
  3V3: Pico_H1.3V3, J1.VCC, S1.1, S1.2, S2.1, S2.2
  N1: Pico_H1.GP16, S2.3, S2.4
  N2: Pico_H1.GP13, J2.pin2
  N3: Pico_H1.GP8, S1.3, S1.4
  N4: Pico_H1.GP1, J1.SCL
  N5: Pico_H1.GP0, J1.SDA

custom parts:
  Raspberry Pi Pico H: Raspberry Pi Pico H. Based around the RP2040 microcontroller the Pico H is a low cost microcontroller device bringing Raspberry Pi quality, cost, and easy of use to the microcontroller space.
  Generic male header - 4 pins: Generic male header
